# Fritzing sketch GATEWAY (saved by Fritzing 0.9.3b)

parts:
  U1 = ESP32-38PinWide [part_number=ESP32-38PinWide]
  SD_card_module1 = SD Card Module
  S1 = Momentary Switch [package=ksa_sealed_tac_switch]
  LED1 = RGB LED (com. cathode, rgb) [package="5 mm [THT]"]
  C1 = Capacitor [package=cap-pth-small2]  # not connected
  R1 = Resistor [tolerance=±5% resistance=10k package="0603 [SMD]"]
  R2 = Resistor [tolerance=±5% resistance=100 package="0603 [SMD]"]
  R3 = Resistor [tolerance=±5% resistance=220 package="0603 [SMD]"]
  R4 = Resistor [tolerance=±5% resistance=220 package="0603 [SMD]"]
  R5 = Resistor [tolerance=±5% resistance=220 package="0603 [SMD]"]

nets:
  N1: U1.GPIO32, R5.Pin_0
  N2: U1.GPIO25, R4.Pin_0
  N3: U1.GPIO26, R3.Pin_0
  N4: U1.GPIO11, LED1.common_cathode
  N5: U1.VIN, SD_card_module1.+5
  N6: U1.GPIO5, SD_card_module1.CS
  N7: U1.GPIO18, SD_card_module1.SCK
  N8: U1.GPIO19, SD_card_module1.MISO
  GND: U1.GND, SD_card_module1.GND
  N9: U1.GPIO23, SD_card_module1.MOSI
  N10: S1.2, R2.Pin_0
  N11: LED1.red_anode, R3.Pin_1
  N12: LED1.green_anode, R4.Pin_1
  N13: LED1.blue_anode, R5.Pin_1
  N14: R1.Pin_0, R2.Pin_1

custom parts:
  ESP32-38PinWide: Generic 38-Pin ESP32 with wide format (only access to one side of pins on a breadboard) based on Stephen Lilley's HiLetgo ESP-WROOM-32 ESP32 ESP-32S Development Board.
  SD Card Module: SD Card Module Slot Socket Reader For Arduino ARM MCU
